// Logisim project 16位快速加法器设计_design.circ as structural Verilog: 7 circuits, main circuit CLA16
module \_8位串行加法器_1  (
  input  [7:0] X,
  input  [7:0] Y,
  input  Cin,
  output [7:0] S,
  output Cout,
  output out_6
);

  wire \n1位全加器_fa1_2_cout , \n1位全加器_fa1_3_cout , \n1位全加器_fa1_4_cout , \n1位全加器_fa1_5_cout ,
       \n1位全加器_fa1_6_cout , \n1位全加器_fa1_7_cout , \n1位全加器_fa1_8_cout ;

  xor xor_1 (out_6, Cout, \n1位全加器_fa1_2_cout );
  \_1位全加器_FA1  \u_1位全加器_fa1_1  (.Cout(Cout), .Si(S[7]), .Cin(\n1位全加器_fa1_2_cout ), .Xi(X[7]), .Yi(Y[7]));
  \_1位全加器_FA1  \u_1位全加器_fa1_2  (.Cout(\n1位全加器_fa1_2_cout ), .Si(S[6]), .Cin(\n1位全加器_fa1_3_cout ), .Xi(X[6]), .Yi(Y[6]));
  \_1位全加器_FA1  \u_1位全加器_fa1_3  (.Cout(\n1位全加器_fa1_3_cout ), .Si(S[5]), .Cin(\n1位全加器_fa1_4_cout ), .Xi(X[5]), .Yi(Y[5]));
  \_1位全加器_FA1  \u_1位全加器_fa1_4  (.Cout(\n1位全加器_fa1_4_cout ), .Si(S[4]), .Cin(\n1位全加器_fa1_5_cout ), .Xi(X[4]), .Yi(Y[4]));
  \_1位全加器_FA1  \u_1位全加器_fa1_5  (.Cout(\n1位全加器_fa1_5_cout ), .Si(S[3]), .Cin(\n1位全加器_fa1_6_cout ), .Xi(X[3]), .Yi(Y[3]));
  \_1位全加器_FA1  \u_1位全加器_fa1_6  (.Cout(\n1位全加器_fa1_6_cout ), .Si(S[2]), .Cin(\n1位全加器_fa1_7_cout ), .Xi(X[2]), .Yi(Y[2]));
  // Probe on X
  // Probe on Y
  // Probe on S
  \_1位全加器_FA1  \u_1位全加器_fa1_7  (.Cout(\n1位全加器_fa1_7_cout ), .Si(S[1]), .Cin(\n1位全加器_fa1_8_cout ), .Xi(X[1]), .Yi(Y[1]));
  // Probe on X
  // Probe on Y
  // Probe on S
  \_1位全加器_FA1  \u_1位全加器_fa1_8  (.Cout(\n1位全加器_fa1_8_cout ), .Si(S[0]), .Cin(Cin), .Xi(X[0]), .Yi(Y[0]));

  // Other names for the same wires on the sheet: OF = out_6

  // Notes on the sheet:
  //   Y: pull=down
  //   Cin: pull=down
  //   X: pull=down
  //   输入引脚区
  //   符号位
  //   输出引脚区
  //   8位串行加法器（1）
  //   Overflow
  //   +
  //   有符号加法
  //   +
  //   =
  //   无符号加法
endmodule

module \_8位串行加法器_2  (
  input  [7:0] X,
  input  [7:0] Y,
  input  Cin,
  output [7:0] S,
  output Cout,
  output out_6
);

  wire \n1位全加器_fa2_2_cout , \n1位全加器_fa2_3_cout , \n1位全加器_fa2_4_cout , \n1位全加器_fa2_5_cout ,
       \n1位全加器_fa2_6_cout , \n1位全加器_fa2_7_cout , \n1位全加器_fa2_8_cout ;

  xor xor_1 (out_6, Cout, \n1位全加器_fa2_2_cout );
  \_1位全加器_FA2  \u_1位全加器_fa2_1  (.Cout(Cout), .Si(S[7]), .Cin(\n1位全加器_fa2_2_cout ), .Xi(X[7]), .Yi(Y[7]));
  \_1位全加器_FA2  \u_1位全加器_fa2_2  (.Cout(\n1位全加器_fa2_2_cout ), .Si(S[6]), .Cin(\n1位全加器_fa2_3_cout ), .Xi(X[6]), .Yi(Y[6]));
  \_1位全加器_FA2  \u_1位全加器_fa2_3  (.Cout(\n1位全加器_fa2_3_cout ), .Si(S[5]), .Cin(\n1位全加器_fa2_4_cout ), .Xi(X[5]), .Yi(Y[5]));
  \_1位全加器_FA2  \u_1位全加器_fa2_4  (.Cout(\n1位全加器_fa2_4_cout ), .Si(S[4]), .Cin(\n1位全加器_fa2_5_cout ), .Xi(X[4]), .Yi(Y[4]));
  \_1位全加器_FA2  \u_1位全加器_fa2_5  (.Cout(\n1位全加器_fa2_5_cout ), .Si(S[3]), .Cin(\n1位全加器_fa2_6_cout ), .Xi(X[3]), .Yi(Y[3]));
  \_1位全加器_FA2  \u_1位全加器_fa2_6  (.Cout(\n1位全加器_fa2_6_cout ), .Si(S[2]), .Cin(\n1位全加器_fa2_7_cout ), .Xi(X[2]), .Yi(Y[2]));
  \_1位全加器_FA2  \u_1位全加器_fa2_7  (.Cout(\n1位全加器_fa2_7_cout ), .Si(S[1]), .Cin(\n1位全加器_fa2_8_cout ), .Xi(X[1]), .Yi(Y[1]));
  // Probe on X
  // Probe on Y
  // Probe on S
  \_1位全加器_FA2  \u_1位全加器_fa2_8  (.Cout(\n1位全加器_fa2_8_cout ), .Si(S[0]), .Cin(Cin), .Xi(X[0]), .Yi(Y[0]));
  // Probe on X
  // Probe on Y
  // Probe on S

  // Other names for the same wires on the sheet: OF = out_6

  // Notes on the sheet:
  //   X: pull=down
  //   Cin: pull=down
  //   Y: pull=down
  //   输入引脚区
  //   符号位
  //   输出引脚区
  //   8位串行加法器（2）
  //   Overflow
  //   +
  //   有符号加法
  //   +
  //   =
  //   无符号加法
endmodule

module \_8位串行可控加减法器_1  (
  input  [7:0] X,
  input  [7:0] Y,
  input  Sub,
  output [7:0] S,
  output Cout,
  output OF
);

  wire \n1位全加器_fa1_2_cout , \n1位全加器_fa1_3_cout , \n1位全加器_fa1_4_cout , \n1位全加器_fa1_5_cout ,
       \n1位全加器_fa1_6_cout , \n1位全加器_fa1_7_cout , \n1位全加器_fa1_8_cout , xor_2_out, xor_3_out, xor_4_out,
       xor_5_out, xor_6_out, xor_7_out, xor_8_out, xor_9_out;
  wire [8:0] \运算指示 ;

  Multiplexer #(.select(1), .width(9), .disabled("Z"), .enable("false")) multiplexer_1 (
    .in0(9'hba), .in1(9'h92), .out(\运算指示 ), .sel(Sub));
  xor xor_1 (OF, Cout, \n1位全加器_fa1_2_cout );
  \_1位全加器_FA1  \u_1位全加器_fa1_1  (.Cout(Cout), .Si(S[7]), .Cin(\n1位全加器_fa1_2_cout ), .Xi(X[7]), .Yi(xor_3_out));
  \_1位全加器_FA1  \u_1位全加器_fa1_2  (
    .Cout(\n1位全加器_fa1_2_cout ), .Si(S[6]), .Cin(\n1位全加器_fa1_3_cout ), .Xi(X[6]), .Yi(xor_2_out));
  xor xor_2 (xor_2_out, Sub, Y[6]);
  xor xor_3 (xor_3_out, Sub, Y[7]);
  \_1位全加器_FA1  \u_1位全加器_fa1_3  (
    .Cout(\n1位全加器_fa1_3_cout ), .Si(S[5]), .Cin(\n1位全加器_fa1_4_cout ), .Xi(X[5]), .Yi(xor_4_out));
  xor xor_4 (xor_4_out, Sub, Y[5]);
  \_1位全加器_FA1  \u_1位全加器_fa1_4  (
    .Cout(\n1位全加器_fa1_4_cout ), .Si(S[4]), .Cin(\n1位全加器_fa1_5_cout ), .Xi(X[4]), .Yi(xor_5_out));
  xor xor_5 (xor_5_out, Sub, Y[4]);
  \_1位全加器_FA1  \u_1位全加器_fa1_5  (
    .Cout(\n1位全加器_fa1_5_cout ), .Si(S[3]), .Cin(\n1位全加器_fa1_7_cout ), .Xi(X[3]), .Yi(xor_7_out));
  xor xor_6 (xor_6_out, Sub, Y[2]);
  xor xor_7 (xor_7_out, Sub, Y[3]);
  \_1位全加器_FA1  \u_1位全加器_fa1_6  (
    .Cout(\n1位全加器_fa1_6_cout ), .Si(S[1]), .Cin(\n1位全加器_fa1_8_cout ), .Xi(X[1]), .Yi(xor_8_out));
  \_1位全加器_FA1  \u_1位全加器_fa1_7  (
    .Cout(\n1位全加器_fa1_7_cout ), .Si(S[2]), .Cin(\n1位全加器_fa1_6_cout ), .Xi(X[2]), .Yi(xor_6_out));
  xor xor_8 (xor_8_out, Sub, Y[1]);
  // Probe on X
  // Probe on Y
  // Probe on S
  \_1位全加器_FA1  \u_1位全加器_fa1_8  (.Cout(\n1位全加器_fa1_8_cout ), .Si(S[0]), .Cin(Sub), .Xi(X[0]), .Yi(xor_9_out));
  xor xor_9 (xor_9_out, Sub, Y[0]);
  DotMatrix #(.inputtype("column"), .matrixcols(3), .matrixrows(3), .persist(0), .dotshape("square")) dotmatrix_1 (
    .col0(\运算指示 [8:6]), .col1(\运算指示 [5:3]), .col2(\运算指示 [2:0]));
  // Probe on X
  // Probe on Y
  // Probe on S

  // Notes on the sheet:
  //   S: pull=down
  //   OF: pull=down
  //   Y: pull=down
  //   Cout: pull=down
  //   Sub: pull=down
  //   X: pull=down
  //   输入引脚区
  //   符号位
  //   输出引脚区
  //   功能说明：8位串行可控加减法器          Sub=0：S=X+Y     Sub=1：S=X-Y        Cout为最高位进位位，OF为有符号溢出标志
  //   8位串行可控加减法器（1）
  //   =
  //   有符号
  //   =
  //   无符号
endmodule

module \_8位串行可控加减法器_2  (
  input  [7:0] X,
  input  [7:0] Y,
  input  Sub,
  output [7:0] S,
  output Cout,
  output OF
);

  wire \n1位全加器_fa2_2_cout , \n1位全加器_fa2_3_cout , \n1位全加器_fa2_4_cout , \n1位全加器_fa2_5_cout ,
       \n1位全加器_fa2_6_cout , \n1位全加器_fa2_7_cout , \n1位全加器_fa2_8_cout , xor_2_out, xor_3_out, xor_4_out,
       xor_5_out, xor_6_out, xor_7_out, xor_8_out, xor_9_out;
  wire [8:0] \运算指示 ;

  Multiplexer #(.select(1), .width(9), .disabled("Z"), .enable("false")) multiplexer_1 (
    .in0(9'hba), .in1(9'h92), .out(\运算指示 ), .sel(Sub));
  xor xor_1 (OF, Cout, \n1位全加器_fa2_2_cout );
  \_1位全加器_FA2  \u_1位全加器_fa2_1  (.Cout(Cout), .Si(S[7]), .Cin(\n1位全加器_fa2_2_cout ), .Xi(X[7]), .Yi(xor_3_out));
  \_1位全加器_FA2  \u_1位全加器_fa2_2  (
    .Cout(\n1位全加器_fa2_2_cout ), .Si(S[6]), .Cin(\n1位全加器_fa2_3_cout ), .Xi(X[6]), .Yi(xor_2_out));
  xor xor_2 (xor_2_out, Sub, Y[6]);
  xor xor_3 (xor_3_out, Sub, Y[7]);
  \_1位全加器_FA2  \u_1位全加器_fa2_3  (
    .Cout(\n1位全加器_fa2_3_cout ), .Si(S[5]), .Cin(\n1位全加器_fa2_4_cout ), .Xi(X[5]), .Yi(xor_4_out));
  \_1位全加器_FA2  \u_1位全加器_fa2_4  (
    .Cout(\n1位全加器_fa2_4_cout ), .Si(S[4]), .Cin(\n1位全加器_fa2_5_cout ), .Xi(X[4]), .Yi(xor_5_out));
  xor xor_4 (xor_4_out, Sub, Y[5]);
  \_1位全加器_FA2  \u_1位全加器_fa2_5  (
    .Cout(\n1位全加器_fa2_5_cout ), .Si(S[3]), .Cin(\n1位全加器_fa2_6_cout ), .Xi(X[3]), .Yi(xor_6_out));
  xor xor_5 (xor_5_out, Sub, Y[4]);
  \_1位全加器_FA2  \u_1位全加器_fa2_6  (
    .Cout(\n1位全加器_fa2_6_cout ), .Si(S[2]), .Cin(\n1位全加器_fa2_7_cout ), .Xi(X[2]), .Yi(xor_7_out));
  xor xor_6 (xor_6_out, Sub, Y[3]);
  xor xor_7 (xor_7_out, Sub, Y[2]);
  \_1位全加器_FA2  \u_1位全加器_fa2_7  (
    .Cout(\n1位全加器_fa2_7_cout ), .Si(S[1]), .Cin(\n1位全加器_fa2_8_cout ), .Xi(X[1]), .Yi(xor_8_out));
  xor xor_8 (xor_8_out, Sub, Y[1]);
  // Probe on X
  // Probe on Y
  // Probe on S
  \_1位全加器_FA2  \u_1位全加器_fa2_8  (.Cout(\n1位全加器_fa2_8_cout ), .Si(S[0]), .Cin(Sub), .Xi(X[0]), .Yi(xor_9_out));
  xor xor_9 (xor_9_out, Sub, Y[0]);
  DotMatrix #(.inputtype("column"), .matrixcols(3), .matrixrows(3), .persist(0), .dotshape("square")) dotmatrix_1 (
    .col0(\运算指示 [8:6]), .col1(\运算指示 [5:3]), .col2(\运算指示 [2:0]));
  // Probe on X
  // Probe on Y
  // Probe on S

  // Notes on the sheet:
  //   Y: pull=down
  //   Cout: pull=down
  //   Sub: pull=down
  //   OF: pull=down
  //   S: pull=down
  //   X: pull=down
  //   输入引脚区
  //   符号位
  //   输出引脚区
  //   功能说明：8位串行可控加减法器          Sub=0：S=X+Y     Sub=1：S=X-Y        Cout为最高位进位位，OF为有符号溢出标志
  //   8位串行可控加减法器（2）
  //   =
  //   有符号
  //   =
  //   无符号
endmodule

// FA1
module \_1位全加器_FA1  (
  input  Cin,
  input  Xi,
  input  Yi,
  output Cout,
  output Si
);

  wire AND_2_out, AND_out, XOR_2_out;

  or OR (Cout, AND_out, AND_2_out);
  and AND (AND_out, Xi, Yi);
  and AND_2 (AND_2_out, Cin, XOR_2_out);
  xor XOR (Si, Cin, XOR_2_out);
  xor XOR_2 (XOR_2_out, Xi, Yi);

  // Notes on the sheet:
  //   Yi: pull=down
  //   Xi: pull=down
  //   Cin: pull=down
  //   Si = Xi ^ Yi ^ Cin
  //   Cout = Xi Yi + Cin (Xi ^ Yi)
  //   1位全加器（FA1）
endmodule

// FA2
module \_1位全加器_FA2  (
  input  Cin,
  input  Xi,
  input  Yi,
  output Cout,
  output Si
);

  wire AND_2_out, AND_3_out, AND_out, XOR_2_out;

  and AND (AND_out, Cin, Xi);
  or OR (Cout, AND_out, AND_2_out, AND_3_out);
  and AND_2 (AND_2_out, Cin, Yi);
  and AND_3 (AND_3_out, Xi, Yi);
  xor XOR (Si, Cin, XOR_2_out);
  xor XOR_2 (XOR_2_out, Xi, Yi);

  // Notes on the sheet:
  //   Cin: pull=down
  //   Yi: pull=down
  //   Xi: pull=down
  //   Si = Xi ^ Yi ^ Cin
  //   Cout = Xi Yi + Cin Xi + Cin Yi
  //   1位全加器（FA2）
endmodule

module CLA16 (
  input  [15:0] A,
  input  [15:0] B,
  input  Cin,
  output [15:0] S,
  output Cout
);

  wire t1a, t2b, t2d, t3a, t3f, t4a, t6b, t6c, t7b, t7c, t9, t62, t99, ta3, tae, tb2;

  buf xor_1 (t1a, A[0]);  // XOR_Gate
  // AND_Gate #(.width(1)) and_1: pin names not known; wires that end beside it: A, t1a, t9
  buf xor_2 (t1a, A[0]);  // XOR_Gate
  buf and_2 (t1a, A[0]);  // AND_Gate
  buf xor_3 (t1a, A[0]);  // XOR_Gate
  buf and_3 (t1a, A[0]);  // AND_Gate
  buf xor_4 (t1a, A[0]);  // XOR_Gate
  // AND_Gate #(.width(1)) and_4: pin names not known; wires that end beside it: A, t1a
  buf xor_5 (t1a, A[0]);  // XOR_Gate
  // AND_Gate #(.width(1)) and_5: pin names not known; wires that end beside it: A, t1a
  buf xor_6 (t1a, t3a);  // XOR_Gate
  // AND_Gate #(.width(1)) and_6: pin names not known; wires that end beside it: t3a, t1a
  buf xor_7 (t1a, t3a);  // XOR_Gate
  // AND_Gate #(.width(1)) and_7: pin names not known; wires that end beside it: t3a, t1a
  buf xor_8 (t1a, t3a);  // XOR_Gate
  // AND_Gate #(.width(1)) and_8: pin names not known; wires that end beside it: t3a, t1a
  buf xor_9 (t1a, t3a);  // XOR_Gate
  // AND_Gate #(.width(1)) and_9: pin names not known; wires that end beside it: t3a, t1a
  buf xor_10 (t1a, t3a);  // XOR_Gate
  // AND_Gate #(.width(1)) and_10: pin names not known; wires that end beside it: t3a, t1a, t6c
  buf xor_11 (t6c, t7c);  // XOR_Gate
  // AND_Gate #(.width(1)) and_11: pin names not known; wires that end beside it: t7c, t6c
  buf xor_12 (t6c, t7c);  // XOR_Gate
  // AND_Gate #(.width(1)) and_12: pin names not known; wires that end beside it: t7c, t6c
  buf xor_13 (t6c, t7c);  // XOR_Gate
  // AND_Gate #(.width(1)) and_13: pin names not known; wires that end beside it: t7c, t6c
  buf xor_14 (t6c, t7c);  // XOR_Gate
  // AND_Gate #(.width(1)) and_14: pin names not known; wires that end beside it: t7c, t6c
  buf xor_15 (t6c, t7c);  // XOR_Gate
  // AND_Gate #(.width(1)) and_15: pin names not known; wires that end beside it: t7c, t6c, ta3
  // XOR_Gate #(.width(1)) xor_16: pin names not known; wires that end beside it: t7c, t6c
  // AND_Gate #(.width(1)) and_16: pin names not known; wires that end beside it: t7c, t6c, tae
  // AND_Gate #(.width(1)) and_17: pin names not known; wires that end beside it: t1a, Cin
  buf xor_17 (S[0], t1a);  // XOR_Gate
  // OR_Gate #(.width(1)) or_1: pin names not known; wires that end beside it: t9, Cin, S
  buf and_18 (S[0], t1a);  // AND_Gate
  buf xor_18 (S[0], t1a);  // XOR_Gate
  buf or_2 (S[0], t1a);  // OR_Gate
  // AND_Gate #(.width(1)) and_19: pin names not known; wires that end beside it: t1a, S
  buf xor_19 (S[0], t1a);  // XOR_Gate
  // OR_Gate #(.width(1)) or_3: pin names not known; wires that end beside it: t1a, S, t2d
  // AND_Gate #(.width(1)) and_20: pin names not known; wires that end beside it: t1a, t2d, t2b
  // XOR_Gate #(.width(1)) xor_20: pin names not known; wires that end beside it: t1a, t2d, S
  // OR_Gate #(.width(1)) or_4: pin names not known; wires that end beside it: t1a, t2b, t3f
  // AND_Gate #(.width(1)) and_21: pin names not known; wires that end beside it: t1a, t3f
  buf xor_21 (t4a, t1a);  // XOR_Gate
  // OR_Gate #(.width(1)) or_5: pin names not known; wires that end beside it: t1a, t3f
  // AND_Gate #(.width(1)) and_22: pin names not known; wires that end beside it: t1a, t3f
  buf xor_22 (t4a, t1a);  // XOR_Gate
  // OR_Gate #(.width(1)) or_6: pin names not known; wires that end beside it: t1a, t3f, t4a
  buf and_23 (t4a, t1a);  // AND_Gate
  buf xor_23 (t4a, t1a);  // XOR_Gate
  // OR_Gate #(.width(1)) or_7: pin names not known; wires that end beside it: t1a, t4a
  // AND_Gate #(.width(1)) and_24: pin names not known; wires that end beside it: t1a, t4a
  buf xor_24 (t4a, t1a);  // XOR_Gate
  // OR_Gate #(.width(1)) or_8: pin names not known; wires that end beside it: t1a, t4a
  // AND_Gate #(.width(1)) and_25: pin names not known; wires that end beside it: t1a, t4a, t62
  buf xor_25 (t4a, t1a);  // XOR_Gate
  // OR_Gate #(.width(1)) or_9: pin names not known; wires that end beside it: t1a, t62, t6b
  // AND_Gate #(.width(1)) and_26: pin names not known; wires that end beside it: t1a, t6b
  buf xor_26 (t7b, t1a);  // XOR_Gate
  // OR_Gate #(.width(1)) or_10: pin names not known; wires that end beside it: t6c, t6b
  // AND_Gate #(.width(1)) and_27: pin names not known; wires that end beside it: t6c, t6b
  buf xor_27 (t7b, t6c);  // XOR_Gate
  // OR_Gate #(.width(1)) or_11: pin names not known; wires that end beside it: t6c, t6b, t7b
  // AND_Gate #(.width(1)) and_28: pin names not known; wires that end beside it: t6c, t7b
  buf xor_28 (t7b, t6c);  // XOR_Gate
  // OR_Gate #(.width(1)) or_12: pin names not known; wires that end beside it: t6c, t7b
  // AND_Gate #(.width(1)) and_29: pin names not known; wires that end beside it: t6c, t7b
  buf xor_29 (t7b, t6c);  // XOR_Gate
  // OR_Gate #(.width(1)) or_13: pin names not known; wires that end beside it: t6c, t7b
  // AND_Gate #(.width(1)) and_30: pin names not known; wires that end beside it: t6c, t7b, t99
  buf xor_30 (t7b, t6c);  // XOR_Gate
  // OR_Gate #(.width(1)) or_14: pin names not known; wires that end beside it: t6c, t99, Cout
  // AND_Gate #(.width(1)) and_31: pin names not known; wires that end beside it: t6c, Cout
  buf xor_31 (t7b, t6c);  // XOR_Gate
  // OR_Gate #(.width(1)) or_15: pin names not known; wires that end beside it: ta3, Cout
  // AND_Gate #(.width(1)) and_32: pin names not known; wires that end beside it: t6c, Cout
  buf xor_32 (tb2, t6c);  // XOR_Gate
  // OR_Gate #(.width(1)) or_16: pin names not known; wires that end beside it: tae, Cout
  // Pins of 1 and 16 bits meet at A
  // Pins of 1 and 16 bits meet at S

  // Other names for the same wires on the sheet: t1[15:0] = B; t29 = t2d; t6d = t6b; t6f = t6b; t7a = t6b; t76 = t6b;
  //   t78 = t6b; t34 = t3f; t36 = t3f; t38 = t3f; t41 = t3f; t43 = t3f; t4c = t4a; t4e = t4a; t4f = t4a; t5a = t4a;
  //   t39 = t4a; t44 = t4a; t55 = t4a; t57 = t4a; t59 = t4a; t60 = t4a; t64 = t4a; t65 = t4a; t3c = t3a; t5b = t3a;
  //   t5d = t3a; t45 = t3a; t47 = t3a; t50 = t3a; t52 = t3a; t66 = t3a; t68 = t3a; t8c = t7b; t8e = t7b; t9b = t7b;
  //   t9c = t7b; t70 = t7b; t81 = t7b; t83 = t7b; t85 = t7b; t86 = t7b; t90 = t7b; t91 = t7b; t97 = t7b; ta7 = t7b;
  //   t7e = t7c; t9d = t7c; t9f = t7c; t71 = t7c; t73 = t7c; t87 = t7c; t89 = t7c; t92 = t7c; t94 = t7c; ta8 = t7c;
  //   taa = t7c; t7d = t6c; t7f = t6c; t8a = t6c; t8b = t6c; t8d = t6c; t8f = t6c; t9a = t6c; t9e = t6c; t72 = t6c;
  //   t74 = t6c; t75 = t6c; t77 = t6c; t79 = t6c; t80 = t6c; t82 = t6c; t84 = t6c; t88 = t6c; t93 = t6c; t95 = t6c;
  //   t96 = t6c; t98 = t6c; ta0 = t6c; ta1 = t6c; ta5 = t6c; ta9 = t6c; tab = t6c; tac = t6c; tb0 = t6c; ta2 = Cout;
  //   ta4 = Cout; ta6 = Cout; tad = Cout; taf = Cout; tb1 = Cout; tb3 = Cout; t8 = Cin; ta = Cin; tc = Cin;
  //   t1e[15:0] = S; t2[15:0] = S; t2e[15:0] = S; t13[15:0] = S; t15[15:0] = S; t17[15:0] = S; t18[15:0] = S;
  //   t20[15:0] = S; t22[15:0] = S; t23[15:0] = S; td[15:0] = S; t0[15:0] = A; t1b[15:0] = A; t2f[15:0] = A;
  //   t3[15:0] = A; t5[15:0] = A; t10[15:0] = A; t19[15:0] = A; t24[15:0] = A; t26[15:0] = A; t31[15:0] = A;
  //   te[15:0] = A; t1c = t1a; t1d = t1a; t1f = t1a; t2a = t1a; t2c = t1a; t3b = t1a; t3d = t1a; t3e = t1a; t4 = t1a;
  //   t4b = t1a; t4d = t1a; t5c = t1a; t5e = t1a; t5f = t1a; t6 = t1a; t6a = t1a; t6e = t1a; t7 = t1a; t11 = t1a;
  //   t12 = t1a; t14 = t1a; t16 = t1a; t21 = t1a; t25 = t1a; t27 = t1a; t28 = t1a; t30 = t1a; t32 = t1a; t33 = t1a;
  //   t35 = t1a; t37 = t1a; t40 = t1a; t42 = t1a; t46 = t1a; t48 = t1a; t49 = t1a; t51 = t1a; t53 = t1a; t54 = t1a;
  //   t56 = t1a; t58 = t1a; t61 = t1a; t63 = t1a; t67 = t1a; t69 = t1a; tb = t1a; tf = t1a
endmodule
